# Fritzing sketch DAB_Radio_v2a (saved by Fritzing 0.9.3b)
circuit board: 7.61804cm x 8.57216cm
breadboards: 3

parts:
  DAB_radio_shield_v1 = Seeeduino Mega
  J2_LED = female pin header, 3 pins [form="♀ (female)"]
  R1 = Resistor [tolerance=±5% resistance=10k package=THT]
  J1_DAB = female pin header, 4 pins [form="♀ (female)"]
  IC2 = Basic FET P-Channel [part_number=IRF5305 package="TO220 [THT]"]
  IC1 = IC, DIP package, 16 pins [chip_label=IC part_number=TDA7053A]
  IC3 = IC, DIP package, 10 pins [chip_label=IC3 part_number=ST3002H5W]
  J3_power = female pin header, 2 pins [form="♀ (female)"]
  R2 = Resistor [tolerance=±5% resistance=1k package=THT]
  C1 = Electrolytic Capacitor [capacitance=220µF package="100 mil [THT, electrolytic]"]
  J4 = female pin header, 3 pins [form="♀ (female)"]
  C2 = Electrolytic Capacitor [capacitance=1µF package="100 mil [THT, electrolytic]"]
  C3 = Electrolytic Capacitor [capacitance=1µF package="100 mil [THT, electrolytic]"]
  C4 = Electrolytic Capacitor [capacitance=1µF package="100 mil [THT, electrolytic]"]
  C5 = Electrolytic Capacitor [capacitance=1µF package="100 mil [THT, electrolytic]"]
  radio = Audio Jack (TRS) 3.5mm [package="PG203J [THT]"]
  aux = Audio Jack (TRS) 3.5mm [package="PG203J [THT]"]
  C7 = Ceramic Capacitor [capacitance=0.47µF package="100 mil [THT, multilayer]"]
  LED1 = LED - 3mm [color="Green (570nm)" package="3 mm [THT]"]
  R3 = Resistor [tolerance=±5% resistance=330 package=THT]
  C8 = Electrolytic Capacitor [capacitance=1µF package="100 mil [THT, electrolytic]"]
  R4 = Resistor [tolerance=±5% resistance=10k package=THT]
  R5 = Resistor [tolerance=±5% resistance=10k package=THT]
  R6 = Resistor [tolerance=±5% resistance=100k package=THT]
  R = Screw terminal - 2 pins [package=THT]
  L = Screw terminal - 2 pins [package=THT]
  J10 = female pin header, 4 pins [form="♀ (female)"]
  J6_I2C = female pin header, 4 pins [form="♀ (female)"]
  J8 = female pin header, 2 pins [form="♀ (female)"]
  R7 = Resistor [tolerance=±5% resistance=8.2k package=THT]
  R8 = Resistor [tolerance=±5% resistance=8.2k package=THT]
  J7 = female pin header, 4 pins [form="♀ (female)"]
  R9 = Resistor [tolerance=±5% resistance=1M package=THT]
  J9 = female pin header, 3 pins [form="♀ (female)"]
  R10 = Resistor [tolerance=±5% resistance=1M package=THT]
  J11 = female pin header, 2 pins [form="♀ (female)"]
  J12 = female pin header, 6 pins [form="♀ (female)"]
  C6 = Ceramic Capacitor [capacitance=0.47µF package="100 mil [THT, multilayer]"]

nets:
  N1: DAB_radio_shield_v1.PWM_12, R2.Pin_1
  N2: DAB_radio_shield_v1.PWM_11, IC3.pin1
  N3: DAB_radio_shield_v1.PWM_7, J9.pin1
  N4: DAB_radio_shield_v1.PWM_5, J1_DAB.pin3
  N5: DAB_radio_shield_v1.PWM_4, J1_DAB.pin4
  N6: DAB_radio_shield_v1.PWM_3, J12.pin1
  N7: DAB_radio_shield_v1.PWM_2, R1.Pin_1
  N8: DAB_radio_shield_v1.5V, J2_LED.pin3, J9.pin3
  N9: DAB_radio_shield_v1.GND, J2_LED.pin2, J8.pin1, J7.pin1
  N10: DAB_radio_shield_v1.A0, J10.pin4
  N11: DAB_radio_shield_v1.A1, J10.pin1
  N12: DAB_radio_shield_v1.A3, J8.pin2, R10.Pin_0
  N13: DAB_radio_shield_v1.A4, J7.pin2, R9.Pin_1
  N14: DAB_radio_shield_v1.A5, J12.pin5
  N15: DAB_radio_shield_v1.A6, J11.pin2
  N16: DAB_radio_shield_v1.A7, J12.pin4
  N17: DAB_radio_shield_v1.I2C_Vcc, J6_I2C.pin1, R7.Pin_0, R8.Pin_0
  N18: DAB_radio_shield_v1.I2C_GND, J6_I2C.pin2, J11.pin1, J12.pin6
  N19: DAB_radio_shield_v1.I2C_SCL_-_21, J6_I2C.pin3, R7.Pin_1
  N20: DAB_radio_shield_v1.I2C_SDA_-_20, J6_I2C.pin4, R8.Pin_1
  N21: DAB_radio_shield_v1.Tx1_-_18, J1_DAB.pin1
  N22: DAB_radio_shield_v1.Rx1_-_19, J1_DAB.pin2
  N23: J2_LED.pin1, R1.Pin_0
  N24: IC2.gate, R2.Pin_0
  N25: IC2.drain, IC1.pin5, C1.+, R3.Pin_0
  N26: IC2.source, J3_power.pin2
  N27: IC1.pin2, IC1.pin8, C8.+, R6.Pin_1, J7.pin4
  N28: IC1.pin4, C7.0
  N29: IC1.pin6, C6.1
  N30: IC1.pin7, IC1.pin10, IC1.pin14, IC3.pin10, J3_power.pin1, C1.-, radio.Sleeve, aux.Sleeve, LED1.cathode, C8.-, R5.Pin_0
  N31: IC1.pin9, L.pin2
  N32: IC1.pin12, L.pin1
  N33: IC1.pin13, R.pin2
  N34: IC1.pin16, R.pin1
  N35: IC3.pin2, C4.-
  N36: IC3.pin3, C6.0
  N37: IC3.pin4, C5.-
  N38: IC3.pin7, C3.-
  N39: IC3.pin8, C7.1
  N40: IC3.pin9, C2.-
  N41: J4.pin1, C2.+, radio.Ring
  N42: J4.pin2, radio.Tip
  N43: J4.pin3, C4.+
  N44: C3.+, aux.Ring
  N45: C5.+, aux.Tip
  N46: LED1.anode, R3.Pin_1
  N47: R4.Pin_0, R5.Pin_1, J7.pin3
  N48: R4.Pin_1, R6.Pin_0
  N49: R9.Pin_0, J9.pin2, R10.Pin_1

notes:
  gnd
  5V
  data
  tx1
  rx1
  shdn
  shnt
  >5V
  mo
  st
  (+)
  (-)
  sda
  scl
  vcc
  vol
  ton1
  ton2
  d7
  sender
  ukw
  spr
  ta
  mw

custom parts:
  Seeeduino Mega: v1.22 Seeeduino Mega is a microntrolller board based on ATmega1280, derived from Arduino Mega with changes in pursuit for small form factor, flexibility and functionality.
  Audio Jack (TRS) 3.5mm: Stereo Jack 2.5mm
